// Logisim project hw2-1.circ as structural Verilog: 1 circuit, main circuit main
module main (
  input  M,
  input  L,
  input  H,
  input  F,
  output out_5
);

  wire and_1_out, and_2_out, and_3_out, and_4_out, or_1_out, or_2_out;

  and and_1 (and_1_out, M, L);
  and and_2 (and_2_out, H, M);
  and and_3 (and_3_out, H, L);
  and and_4 (and_4_out, L, F);
  or or_1 (or_1_out, and_1_out, and_2_out);
  or or_2 (or_2_out, and_3_out, and_4_out);
  or or_3 (out_5, or_1_out, or_2_out);
endmodule
