// Logisim project hw2-2.circ as structural Verilog: 1 circuit, main circuit main
module main (
  input  M,
  input  L,
  input  H,
  input  F,
  output out_5
);

  wire nand_1_out, nand_2_out, nand_3_out, nand_4_out, nand_5_out, nand_6_out, nand_7_out, nand_8_out;

  nand nand_1 (nand_1_out, M, L);
  nand nand_2 (nand_2_out, H, M);
  nand nand_3 (nand_3_out, H, L);
  nand nand_4 (nand_4_out, L, F);
  nand nand_5 (nand_5_out, nand_1_out, nand_2_out);
  nand nand_6 (nand_6_out, nand_3_out, nand_4_out);
  nand nand_7 (nand_7_out, nand_5_out, nand_5_out);
  nand nand_8 (nand_8_out, nand_6_out, nand_6_out);
  nand nand_9 (out_5, nand_7_out, nand_8_out);
endmodule
