// Logisim project hw4_FurkanSalik_150200056.circ as structural Verilog: 1 circuit, main circuit main
module main (
  input  [3:0] A,
  input  [3:0] B,
  input  [3:0] C,
  input  Y,
  input  X,
  output [3:0] Z
);

  wire and_1_out;
  wire [3:0] multiplexer_1_out, multiplexer_2_out, multiplexer_3_out, not_1_out;

  assign not_1_out = ~C;  // NOT_Gate not_1, 4 bits wide
  Multiplexer #(.width(4)) multiplexer_1 (.in0(not_1_out), .in1(C), .out(multiplexer_1_out), .sel(Y));  // open: en
  Multiplexer #(.width(4)) multiplexer_2 (.in0(A), .in1(4'b0000), .out(multiplexer_2_out), .sel(Y));  // open: en
  Multiplexer #(.width(4)) multiplexer_3 (
    .in0(B), .in1(multiplexer_1_out), .out(multiplexer_3_out), .sel(X));  // open: en
  and and_1 (and_1_out, X, ~Y);  // AND_Gate
  Adder #(.width(4)) adder_1 (.a(multiplexer_2_out), .b(multiplexer_3_out), .out(Z), .cin(and_1_out));  // open: cout

  // Notes on the sheet:
  //   Furkan Salık
  //   150200056
endmodule
