// Logisim project part4.circ as structural Verilog: 1 circuit, main circuit main
module main (
  input  J,
  input  K,
  input  J_2,
  input  K_2,
  input  J_3,
  input  K_3,
  input  Q,
  output S,
  output R
);

  wire and_1_out, and_2_out, and_3_out, and_4_out, and_5_out, not_1_out, not_2_out;

  not not_1 (not_1_out, K);
  not not_2 (not_2_out, J_2);
  and and_1 (and_1_out, J, not_1_out);
  and and_2 (and_2_out, not_2_out, K_2);
  and and_3 (and_3_out, J_3, K_3);
  not not_3 (Q, Q);
  and and_4 (and_4_out, and_3_out, Q);
  and and_5 (and_5_out, Q, and_3_out);
  or or_1 (S, and_1_out, and_4_out);
  or or_2 (R, and_2_out, and_5_out);
endmodule
